// Logisim project Exercicio_1202.circ as structural Verilog: 4 circuits, main circuit main
module main (
  input  w_r,
  input  \endereço ,
  input  clock,
  input  clear,
  input  [3:0] entrada,
  output [3:0] saida
);

  ram_1x4 ram_1x4_1 (
    .w_r(w_r), .clock(clock), .clear(clear), .\endereço (\endereço ), .entrada(entrada), .saida(saida));
endmodule

module Ram (
  input  \endreço ,
  input  R_W,
  input  clk,
  input  \input ,
  input  clr,
  output out_6
);

  wire and_1_out, j_k_ff_1_q, not_1_out;

  and and_1 (and_1_out, \endreço , R_W, clk);
  not not_1 (not_1_out, \input );
  J_K_Flip_Flop j_k_ff_1 (
    .J(\input ), .clk(and_1_out), .K(not_1_out), .Q(j_k_ff_1_q), .reset(clr));  // open: Qn, preset, en
  and and_2 (out_6, \endreço , j_k_ff_1_q);
endmodule

module ram_1x4 (
  input  \endereço ,
  input  w_r,
  input  clock,
  input  clear,
  input  [3:0] entrada,
  output [3:0] saida
);

  Ram_1X2 ram_1x2_1 (
    .w_r(w_r), .clock(clock), .clear(clear), .in_1(\endereço ), .out_6(saida[3:2]), .in_5(entrada[3:2]));
  Ram_1X2 ram_1x2_2 (
    .w_r(w_r), .clock(clock), .clear(clear), .in_1(\endereço ), .out_6(saida[1:0]), .in_5(entrada[1:0]));
endmodule

module Ram_1X2 (
  input  in_1,
  input  w_r,
  input  clock,
  input  clear,
  input  [1:0] in_5,
  output [1:0] out_6
);

  Ram ram_1 (.R_W(w_r), .clk(clock), .clr(clear), .\endreço (in_1), .out_6(out_6[1]), .\input (in_5[1]));
  Ram ram_2 (.R_W(w_r), .clk(clock), .clr(clear), .\endreço (in_1), .out_6(out_6[0]), .\input (in_5[0]));
endmodule
